# Fritzing sketch ThunderWatcher (saved by Fritzing 0.9.3b)
breadboards: 1

parts:
  パーツ2 = Arduino Nano (Rev3.0) (ICSP)
  パーツ3 = LilyPad Coin Cell Battery Holder
  S1 = Toggle Switch [package=THT]
  パーツ4 = LilyPad Coin Cell Battery Holder
  J1 = female pin header, 5 pins [form="♀ (female)"]
  J2 = female pin header, 5 pins [form="♀ (female)"]
  LED1 = LED - 5mm [color="Red (633nm)" package="5 mm [THT]"]
  R1 = Resistor [tolerance=±5% resistance=150 package=THT]
  J3 = female pin header, 5 pins [form="♀ (female)"]
  J4 = female pin header, 5 pins [form="♀ (female)"]

nets:
  N1: パーツ2.GND, S1.L2, J1.pin4, J2.pin5, LED1.cathode, J3.pin4, J4.pin5
  N2: パーツ2.D4, R1.Pin_1
  N3: パーツ2.D5, J1.pin3, J3.pin3
  N4: パーツ2.VIN, パーツ3.+
  N5: パーツ2.5V, J1.pin5, J3.pin5
  N6: パーツ2.A5, J1.pin2, J2.pin3, J3.pin2, J4.pin3
  N7: パーツ2.A4, J1.pin1, J2.pin4, J3.pin1, J4.pin4
  N8: パーツ2.3V3, J2.pin1, J2.pin2, J4.pin1, J4.pin2
  N9: パーツ3.-, パーツ4.+
  N10: S1.COM, パーツ4.-

notes:
  AQM0802
  AS3935
